# Fritzing sketch Derby Car - Trinket (saved by Fritzing 0.9.3b)
breadboards: 1

parts:
  Part2 = Adafruit Switched JST Breakout [part_number="Adafruit #1863"]
  Part3 = Adafruit LIS3DH [part_number="Adafruit #2809"]
  U1 = LIPO-110mAh [package=lipo-110]  # not connected
  Part4 = NeoPixel Jewel [part_number=2226]
  Part5 = NeoPixel Stick [part_number=1426]
  Part6 = NeoPixel Stick [part_number=1426]
  Part7 = Adafruit Pro Trinket 5V 16MHz [part_number="Adafruit #2000"]  # not connected

nets:
  GND: Part2.GND, Part3.GND, Part4.GND, Part5.GND, Part6.GND
  +5V: Part2.SW, Part3.VIN, Part4.VDD, Part5.+5V, Part6.+5V
  N1: Part4.IN, Part6.DATAOUT
  N2: Part5.DATAOUT, Part6.DATAIN

custom parts:
  Adafruit Switched JST Breakout: This switched JST connector is the best way to quickly prototype with our LiPoly batteries. We paired a genuine JST connector with a slide switch that can do up to 600mA. Both are soldered onto a breadboard-friendly breakout. There's two ground pins, one 'switched' power pin, and one pin that is always on. This is compatible with the "JST PH 2-pin" connectors we use in our battery packs..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
  Adafruit LIS3DH: The LIS3DH is a very popular low power triple-axis accelerometer. It's low-cost, but has just about every 'extra' you'd want in an accelerometer: Three axis sensing, 10-bit precision ±2g/±4g/±8g/±16g selectable scaling Both I2C (2 possible addresses) and SPI interface options Interrupt output Multiple data rate options 1 Hz to 5Khz As low as 2uA current draw (just the chip itself, not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
  NeoPixel Jewel: We fit seven of our tiny 5050 (5mm x 5mm) smart RGB LEDs onto a beautiful, round PCB with mounting holes and a chainable design to create what we think is our most elegant (and evening-wear appropriate) NeoPixel board yet. Use only one microcontroller pin to control as many as you can chain together! Each LED is addressable as the driver chip is inside the LED. Each one has ~18mA constant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
  NeoPixel Stick: Make your own little LED strip arrangement with this stick of NeoPixel LEDs. We crammed 8 of the tiny 5050 (5mm x 5mm) smart RGB LEDs onto a PCB with mounting holes and a chainable design. Use only one microcontroller pin to control as many as you can chain together! Each LED is addressable as the driver chip is inside the LED. Each one has ~18mA constant current drive so the color will be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
  Adafruit Pro Trinket 5V 16MHz: Trinket's got a big sister in town - the Pro Trinket 5V! Pro Trinket combines everything you love about Trinket with the familiarity of the common core Arduino chip, the ATmega328. It's like an Arduino Pro Mini with more pins and USB tossed in, so delicious. Trinket's a year old now, and while its been great to see tons of tiny projects, sometimes you just need more pins, more FLASH, and more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
